# Fritzing sketch self_driving_fritz (saved by Fritzing 0.9.2b)

parts:
  Part1 = Arduino Uno (Rev3)
  Part3 = Triple Axis Magnetometer - HMC5883 Breakout
  Motor2 = DC Motor
  SONAR1 = Maxbotix MaxSonar Ultrasonic Sensor (Hi-Res)
  BATT1 = 4xAA Switchable Battery Pack w/JST connector
  Part4 = Adafruit DRV8871 [part_number="Adafruit #3190"]
  Servo1 = Basic Servo
  Servo2 = Basic Servo
  C1 = Electrolytic Capacitor [capacitance=1µF package="100 mil [THT, electrolytic]"]

nets:
  N1: Part1.A0, SONAR1.AN
  N2: Part1.A4/SDA, Part3.SDA
  N3: Part1.A5/SCL, Part3.SCL
  N4: Part1.D11_PWM/MOSI, Part4.IN2
  GND: Part1.GND, Part3.GND, SONAR1.GND, BATT1.NEG, Part4.GND, Servo2.gnd, C1.-
  N5: Part1.D2, Servo1.pulse
  N6: Part1.D3_PWM, Part4.IN1
  N7: Part1.D4, Servo2.pulse
  5V: Part1.5V, Part3.VCC, SONAR1.+5V
  N8: Motor2.pin_1, Part4.OUT2
  N9: Motor2.pin_2, Part4.OUT1
  N10: BATT1.POS, Part4.VMOTOR, C1.+

custom parts:
  Maxbotix MaxSonar Ultrasonic Sensor (Hi-Res): Maxbotix MaxSonar Hi-Resolution Ultrasonic Sensor HRLV-EZ0, HRLV-EZ1, HRLV-EZ2, HRLV-EZ3, HRLV-EZ4
  4xAA Switchable Battery Pack w/JST connector: 4xAA Switchable Battery Pack with JST connector
  Adafruit DRV8871: Crank up your robotics with powerful Adafruit DRV8871 motor driver breakout board. This motor driver has a lot of great specs that make it useful for a wide variety of mechatronics. In particular, the simple resistor-set current limiting and auto-magic PWM support make it super easy to use. Check out the specs for the DRV8871: 6.5V to 45V motor power voltage Up to 5.5V logic level on IN pins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
